# Fritzing sketch wemos_dht22 (saved by Fritzing 0.9.3b)

parts:
  WeMos_D1_Mini1 = WeMos D1 Mini
  RHT1 = Humidity and Temperature Sensor RHT03
  R1 = Resistor [tolerance=±5% resistance=10k package=THT]

nets:
  N1: WeMos_D1_Mini1.D0, WeMos_D1_Mini1.RST
  N2: WeMos_D1_Mini1.D3, R1.Pin_0
  N3: WeMos_D1_Mini1.G, RHT1.GND_1, RHT1.GND_2
  N4: RHT1.Vcc, RHT1.Data-signal, R1.Pin_1
